// Logisim project SR_latch.circ as structural Verilog: 1 circuit, main circuit main
module main (
  input  S,
  input  R,
  output Q_not,
  output Qt
);

  nand nand_1 (Q_not, S, Qt);
  nand nand_2 (Qt, Q_not, R);
endmodule
